// Logisim project PROCESSADOR.circ as structural Verilog
// OP
module main (
);

  wire and_1_out, button_1_out, comparator_1_eq, or_1_out, uc_1_beq, uc_1_j_inst, uc_1_reg_write;
  wire [1:0] uc_1_ula_op;
  wire [7:0] adder_1_out, multiplexer_1_out, register_1_q;
  wire [31:0] banco_de_registradores_1_rs_out, banco_de_registradores_1_rt_out, ram_1_data;

  Comparator #(.width(32)) comparator_1 (
    .a(banco_de_registradores_1_rt_out), .b(banco_de_registradores_1_rs_out), .eq(comparator_1_eq));  // open: gt, lt
  Adder adder_1 (.a(register_1_q), .b(8'h4), .out(adder_1_out));  // open: cin, cout
  and and_1 (and_1_out, comparator_1_eq, uc_1_beq);
  Button button_1 (.out(button_1_out));
  Register register_1 (.D(adder_1_out), .Q(register_1_q), .clk(button_1_out));  // open: en, clr
  or or_1 (or_1_out, and_1_out, uc_1_j_inst);
  Multiplexer #(.width(8), .enable("false")) multiplexer_1 (
    .in0(register_1_q), .in1(8'h4), .out(multiplexer_1_out), .sel(or_1_out));
  RAM #(.dataWidth(32), .bus("separate")) ram_1 (
    .addr(multiplexer_1_out), .data(ram_1_data), .clk(button_1_out));  // open: din, str, sel, ld, clr
  Banco_de_Registradores banco_de_registradores_1 (
    .RT_OUT(banco_de_registradores_1_rt_out), .RS_OUT(banco_de_registradores_1_rs_out),
    .REG_WRITE(uc_1_reg_write));  // open: INPUT_VALUE, RD, CLK, RS, RT, RESET
  UC uc_1 (
    .OPCODE(ram_1_data[2:0]), .ULA_OP(uc_1_ula_op), .REG_WRITE(uc_1_reg_write), .J_INST(uc_1_j_inst),
    .BEQ(uc_1_beq));  // open: READ_MEMORY, WRITE_MEMORY
  ULA ula_1 (
    .RT(banco_de_registradores_1_rt_out), .RS(banco_de_registradores_1_rs_out));  // open: SAÍDA, OP_CODE, IMMEDIATE
endmodule

// BR
module Banco_de_Registradores (
  input  [31:0] INPUT_VALUE,
  input  [4:0] RT,
  input  [4:0] RD,
  input  [4:0] RS,
  input  CLK,
  input  RESET,
  input  REG_WRITE,
  output [31:0] RT_OUT,
  output [31:0] RS_OUT
);

  wire _1, _2, _3, _4, _5, _6, _7, _8, _9, _10, _11, _12, _13, _14, _15, _16, _17, _18, _19, _20, _21, _22,
       _23, _24, _25, _26, _27, _28, _29, _30, _31, and_2_out, and_3_out, and_4_out, and_5_out, and_6_out,
       and_7_out, and_8_out, and_9_out, and_10_out, and_11_out, and_12_out, and_13_out, and_14_out,
       and_15_out, and_16_out, and_17_out, and_18_out, and_19_out, and_20_out, and_21_out, and_22_out,
       and_23_out, and_24_out, and_25_out, and_26_out, and_27_out, and_28_out, and_29_out, and_30_out,
       and_31_out, and_32_out, CLK_t;
  wire [31:0] S0, S1, S2, S3, S4, S5, S6, S7, S8, S9, S10, S11, S12, S13, S14, S15, S16, S17, S18, S19, S20,
       S21, S22, S23, S24, S25, S26, S27, S28, S29, S30, S31, S230;

  Demultiplexer #(.select(5), .enable("false")) demultiplexer_1 (
    .out1(_1), .out2(_2), .out3(_3), .out4(_4), .out5(_5), .out6(_6), .out7(_7), .out8(_8), .out9(_9),
    .out10(_10), .out11(_11), .out12(_12), .out13(_13), .out14(_14), .out15(_15), .out16(_16), .out17(_17),
    .out18(_18), .out19(_19), .out20(_20), .out21(_21), .out22(_22), .out23(_23), .out24(_24), .out25(_25),
    .out26(_26), .out27(_27), .out28(_28), .out29(_29), .out30(_30), .out31(_31), .in(1'b1), .sel(RD));  // open: out0
  and and_1 (CLK_t, CLK, REG_WRITE);
  Register #(.width(32)) R0 (.Q(S0));  // open: D, en, clk, clr
  Register #(.width(32)) R8 (.D(INPUT_VALUE), .Q(S8), .clk(and_2_out), .clr(RESET));  // open: en
  and and_2 (and_2_out, _8, CLK_t);
  Register #(.width(32)) R16 (.D(INPUT_VALUE), .Q(S16), .clk(and_3_out), .clr(RESET));  // open: en
  and and_3 (and_3_out, _16, CLK_t);
  Register #(.width(32)) R24 (.D(INPUT_VALUE), .Q(S24), .clk(and_4_out), .clr(RESET));  // open: en
  and and_4 (and_4_out, _24, CLK_t);
  and and_5 (and_5_out, _1, CLK_t);
  and and_6 (and_6_out, _9, CLK_t);
  and and_7 (and_7_out, _17, CLK_t);
  and and_8 (and_8_out, _25, CLK_t);
  Register #(.width(32)) R1 (.D(INPUT_VALUE), .Q(S1), .clk(and_5_out), .clr(RESET));  // open: en
  and and_9 (and_9_out, _2, CLK_t);
  Register #(.width(32)) R9 (.D(INPUT_VALUE), .Q(S9), .clk(and_6_out), .clr(RESET));  // open: en
  and and_10 (and_10_out, _10, CLK_t);
  Register #(.width(32)) R17 (.D(INPUT_VALUE), .Q(S17), .clk(and_7_out), .clr(RESET));  // open: en
  and and_11 (and_11_out, _18, CLK_t);
  Register #(.width(32)) R25 (.D(INPUT_VALUE), .Q(S25), .clk(and_8_out), .clr(RESET));  // open: en
  and and_12 (and_12_out, _26, CLK_t);
  Register #(.width(32)) R2 (.D(INPUT_VALUE), .Q(S2), .clk(and_9_out), .clr(RESET));  // open: en
  Register #(.width(32)) R10 (.D(INPUT_VALUE), .Q(S10), .clk(and_10_out), .clr(RESET));  // open: en
  Register #(.width(32)) R18 (.D(INPUT_VALUE), .Q(S18), .clk(and_11_out), .clr(RESET));  // open: en
  Register #(.width(32)) R26 (.D(INPUT_VALUE), .Q(S26), .clk(and_12_out), .clr(RESET));  // open: en
  Register #(.width(32)) R3 (.D(INPUT_VALUE), .Q(S3), .clk(and_13_out), .clr(RESET));  // open: en
  and and_13 (and_13_out, _3, CLK_t);
  Register #(.width(32)) R11 (.D(INPUT_VALUE), .Q(S11), .clk(and_14_out), .clr(RESET));  // open: en
  and and_14 (and_14_out, _11, CLK_t);
  Register #(.width(32)) R19 (.D(INPUT_VALUE), .Q(S19), .clk(and_15_out), .clr(RESET));  // open: en
  and and_15 (and_15_out, _19, CLK_t);
  Register #(.width(32)) R27 (.D(INPUT_VALUE), .Q(S27), .clk(and_16_out), .clr(RESET));  // open: en
  and and_16 (and_16_out, _27, CLK_t);
  Register #(.width(32)) R4 (.D(INPUT_VALUE), .Q(S4), .clk(and_17_out), .clr(RESET));  // open: en
  and and_17 (and_17_out, _4, CLK_t);
  Register #(.width(32)) R12 (.D(INPUT_VALUE), .Q(S12), .clk(and_18_out), .clr(RESET));  // open: en
  and and_18 (and_18_out, _12, CLK_t);
  Register #(.width(32)) R20 (.D(INPUT_VALUE), .Q(S20), .clk(and_19_out), .clr(RESET));  // open: en
  and and_19 (and_19_out, _20, CLK_t);
  Register #(.width(32)) R28 (.D(INPUT_VALUE), .Q(S28), .clk(and_20_out), .clr(RESET));  // open: en
  and and_20 (and_20_out, _28, CLK_t);
  Register #(.width(32)) R5 (.D(INPUT_VALUE), .Q(S5), .clk(and_21_out), .clr(RESET));  // open: en
  and and_21 (and_21_out, _5, CLK_t);
  Register #(.width(32)) R13 (.D(INPUT_VALUE), .Q(S13), .clk(and_22_out), .clr(RESET));  // open: en
  and and_22 (and_22_out, _13, CLK_t);
  Register #(.width(32)) R21 (.D(INPUT_VALUE), .Q(S21), .clk(and_23_out), .clr(RESET));  // open: en
  and and_23 (and_23_out, _21, CLK_t);
  Register #(.width(32)) R29 (.D(INPUT_VALUE), .Q(S29), .clk(and_24_out), .clr(RESET));  // open: en
  and and_24 (and_24_out, _29, CLK_t);
  Register #(.width(32)) R6 (.D(INPUT_VALUE), .Q(S6), .clk(and_25_out), .clr(RESET));  // open: en
  and and_25 (and_25_out, _6, CLK_t);
  Register #(.width(32)) R14 (.D(INPUT_VALUE), .Q(S14), .clk(and_26_out), .clr(RESET));  // open: en
  and and_26 (and_26_out, _14, CLK_t);
  Register #(.width(32)) R22 (.D(INPUT_VALUE), .Q(S22), .clk(and_27_out), .clr(RESET));  // open: en
  and and_27 (and_27_out, _22, CLK_t);
  Register #(.width(32)) R30 (.D(INPUT_VALUE), .Q(S230), .clk(and_28_out), .clr(RESET));  // open: en
  and and_28 (and_28_out, _30, CLK_t);
  Register #(.width(32)) R7 (.D(INPUT_VALUE), .Q(S7), .clk(and_29_out), .clr(RESET));  // open: en
  and and_29 (and_29_out, _7, CLK_t);
  Register #(.width(32)) R15 (.D(INPUT_VALUE), .Q(S15), .clk(and_30_out), .clr(RESET));  // open: en
  and and_30 (and_30_out, _15, CLK_t);
  Register #(.width(32)) R23 (.D(INPUT_VALUE), .Q(S23), .clk(and_31_out), .clr(RESET));  // open: en
  and and_31 (and_31_out, _23, CLK_t);
  Register #(.width(32)) R31 (.D(INPUT_VALUE), .Q(S31), .clk(and_32_out), .clr(RESET));  // open: en
  and and_32 (and_32_out, _31, CLK_t);
  Multiplexer #(.select(5), .width(32), .enable("false")) multiplexer_1 (
    .in0(S0), .in1(S1), .in2(S2), .in3(S3), .in4(S4), .in5(S5), .in6(S6), .in7(S7), .in8(S8), .in9(S9),
    .in10(S10), .in11(S11), .in12(S12), .in13(S13), .in14(S14), .in15(S15), .in16(S16), .in17(S17),
    .in18(S18), .in19(S19), .in20(S20), .in21(S21), .in22(S22), .in23(S23), .in24(S24), .in25(S25),
    .in26(S26), .in27(S27), .in28(S28), .in29(S29), .in30(S30), .in31(S31), .out(RT_OUT), .sel(RT));
  Multiplexer #(.select(5), .width(32), .enable("false")) multiplexer_2 (
    .in0(S0), .in1(S1), .in2(S2), .in3(S3), .in4(S4), .in5(S5), .in6(S6), .in7(S7), .in8(S8), .in9(S9),
    .in10(S10), .in11(S11), .in12(S12), .in13(S13), .in14(S14), .in15(S15), .in16(S16), .in17(S17),
    .in18(S18), .in19(S19), .in20(S20), .in21(S21), .in22(S22), .in23(S23), .in24(S24), .in25(S25),
    .in26(S26), .in27(S27), .in28(S28), .in29(S29), .in30(S30), .in31(S31), .out(RS_OUT), .sel(RS));
endmodule

module ULA (
  input  [31:0] RT,
  input  [31:0] RS,
  input  [15:0] IMMEDIATE,
  input  [1:0] OP_CODE,
  output [31:0] \SAÍDA 
);

  wire [31:0] adder_1_out, adder_2_out, conversor_16_32_1_saida, multiplier_1_out, multiplier_2_out;

  CONVERSOR_16____32 conversor_16_32_1 (.INPUT(IMMEDIATE), .SAIDA(conversor_16_32_1_saida));
  Adder #(.width(32)) adder_1 (.a(RT), .b(RS), .out(adder_1_out));  // open: cin, cout
  Multiplier #(.width(32)) multiplier_1 (.a(RT), .b(RS), .out(multiplier_1_out));  // open: cin, cout
  Adder #(.width(32)) adder_2 (.a(RT), .b(conversor_16_32_1_saida), .out(adder_2_out));  // open: cin, cout
  Multiplier #(.width(32)) multiplier_2 (
    .a(RT), .b(conversor_16_32_1_saida), .out(multiplier_2_out));  // open: cin, cout
  Multiplexer #(.select(2), .width(32), .enable("false")) multiplexer_1 (
    .in0(adder_1_out), .in1(multiplier_1_out), .in2(adder_2_out), .in3(multiplier_2_out), .out(\SAÍDA ),
    .sel(OP_CODE));
endmodule

// CONV
module CONVERSOR_16____32 (
  input  [15:0] INPUT,
  output [31:0] SAIDA
);


  assign SAIDA = {{16{1'b0}}, INPUT};
endmodule

module UC (
  input  [2:0] OPCODE,
  output [1:0] ULA_OP,
  output REG_WRITE,
  output J_INST,
  output BEQ,
  output READ_MEMORY,
  output WRITE_MEMORY
);

  wire and_1_out, not_1_out, not_2_out, not_3_out, not_4_out, not_5_out, not_6_out;

  not not_1 (not_1_out, OPCODE[1]);
  not not_2 (not_2_out, OPCODE[2]);
  not not_3 (not_3_out, OPCODE[1]);
  not not_4 (not_4_out, OPCODE[1]);
  not not_5 (not_5_out, OPCODE[2]);
  not not_6 (not_6_out, OPCODE[0]);
  and and_1 (and_1_out, not_1_out, OPCODE[2]);
  and and_2 (J_INST, OPCODE[0], OPCODE[1], OPCODE[2]);
  and and_3 (BEQ, OPCODE[0], OPCODE[1], not_2_out);
  and and_4 (READ_MEMORY, OPCODE[0], not_3_out, OPCODE[2]);
  and and_5 (WRITE_MEMORY, OPCODE[0], not_4_out, not_5_out);
  or or_1 (REG_WRITE, not_6_out, and_1_out);

  assign ULA_OP = OPCODE[2:1];
endmodule
